# Fritzing sketch rangkaian (saved by Fritzing 0.9.3b)

parts:
  Part1 = Arduino Uno (Rev3) - ICSP
  DRV_1 = DRV 8825 Stepper Motor Carrier, High Current [part_number="DRV 8825"]  # not connected
  M1 = Stepper Motor - Unipolar
  DRV_2 = DRV 8825 Stepper Motor Carrier, High Current [part_number="DRV 8825"]  # not connected
  M2 = Stepper Motor - Unipolar
  Arduino_CNC_Shield_V3_00_1 = Arduino_CNC_V3.00
  LoRa_Module1 = Ra-01 - LoRa Module SX1278 [part_number=SX1278]
  U1 = RELAY [package=relay-t9a]
  Q1 = TRANSISTOR_NPN [package=to-92]
  R1 = Resistor [tolerance=±5% resistance=220 package="1206 [SMD]"]  # not connected
  R2 = Resistor [tolerance=±5% resistance=220 package="1206 [SMD]"]
  ANT1 = Antenna
  WATER_PUMP1 = water pump/motor
  Power_plug1 = Power plug
  Power_plug2 = Power plug

nets:
  N1: Part1.ICSP_MISO, Part1.D12/MISO, Arduino_CNC_Shield_V3_00_1.End_Stops_Y+_(and_Y-), LoRa_Module1.NSS
  N2: Part1.5V, Arduino_CNC_Shield_V3_00_1.End_Stops_Y+_(Gnd)
  N3: Part1.ICSP_SCK, Part1.D13/SCK
  N4: Part1.ICSP_MOSI, Part1.D11_PWM/MOSI, Arduino_CNC_Shield_V3_00_1.End_Stops_Y-_(Gnd)
  N5: Part1.RESET, Arduino_CNC_Shield_V3_00_1.End_Stops_X+_(and_X-), LoRa_Module1.GND#1
  N6: Part1.GND, Arduino_CNC_Shield_V3_00_1.End_Stops_X+_(Gnd)
  N7: M1.A, Arduino_CNC_Shield_V3_00_1.X-MTR_'4'
  N8: M1.C, Arduino_CNC_Shield_V3_00_1.X-MTR_'3'
  N9: M1.B, Arduino_CNC_Shield_V3_00_1.X-MTR_'2'
  N10: M1.D, Arduino_CNC_Shield_V3_00_1.X-MTR_'1'
  N11: M2.A, Arduino_CNC_Shield_V3_00_1.Y-MTR_'4'
  N12: M2.C, Arduino_CNC_Shield_V3_00_1.Y-MTR_'3'
  N13: M2.B, Arduino_CNC_Shield_V3_00_1.Y-MTR_'2'
  N14: M2.D, Arduino_CNC_Shield_V3_00_1.Y-MTR_'1'
  N15: Arduino_CNC_Shield_V3_00_1.POWER_-, Power_plug1.GND
  N16: Arduino_CNC_Shield_V3_00_1.POWER_+, Power_plug1.VCC
  N17: Arduino_CNC_Shield_V3_00_1.GND, LoRa_Module1.GND#10
  3V3: Arduino_CNC_Shield_V3_00_1.3V3, LoRa_Module1.3.3V
  N18: Arduino_CNC_Shield_V3_00_1.End_Stops_Z+_(and_Z-)_/_SpnEn, LoRa_Module1.MOSI
  N19: Arduino_CNC_Shield_V3_00_1.SpnEn_/_Z_Limit, LoRa_Module1.MISO
  N20: Arduino_CNC_Shield_V3_00_1.SpnDir, LoRa_Module1.SCK
  N21: Arduino_CNC_Shield_V3_00_1.CoolEn, LoRa_Module1.DIO0
  N22: Arduino_CNC_Shield_V3_00_1.Resume, LoRa_Module1.DIO1
  N23: LoRa_Module1.ANT, ANT1.antenna_lead
  N24: U1.COIL1, U1.NO, Power_plug2.VCC
  N25: U1.COIL2, WATER_PUMP1.pin_2
  N26: U1.MAIN, Q1.C
  N27: Q1.E, R2.Pin_1, WATER_PUMP1.pin_1, Power_plug2.GND
  N28: Q1.B, R2.Pin_0

notes:
  R 100 K
  R 1 K
  Transistor NPN
  Power Supply 12 V
  Power Supply 24 V
  Relay SPDT
  Water Pump
  LoRa SX1278
  Antenna
  Stepper Motor Nema 17
  Arduino Uno + CNC Shield V3

custom parts:
  Arduino_CNC_V3.00: Protoneer Arduino CNC Shield V3.00 If using Grbl V0.9: The “A” axis can not be used (yet). The “SCL” (Arduino A5) pin is now used for 'Probing' input. The “End Stops Z+ & Z-” (Arduino D11) and “SpnEn” (Arduino D12) have been switched!
  Ra-01 - LoRa Module SX1278: The Ra-01 LoRa Module featuring the SX1278 engine by Semtech. Module by AI-Thinker. Module (Ra-01) specifications from: https://www.banggood.com/Ra-01-Smart-Electronics-SX1278-LoRa-Spread-Spectrum-Wireless-Module-Ultra-Far-10KM-433M-p-1130769.html Description: Power supply: DC1.8-3.7V(3.3V) Chip: SX1278 Frequency: 433Mhz Operating temperature: -40~+85°C On Sheild Description (may vary by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
  water pump/motor: WATER PUMP BY ARDUBLOCKTR
